// Digital circuit Yiğit Çetin Example-Circuit.dig as structural Verilog
module \Yiğit_Çetin_Example_Circuit  (
  input  in_1,
  input  in_2,
  input  in_3,
  output out_4,
  output out_5,
  output out_6
);

  nor nor_1 (out_4, in_1, in_2);
  or or_1 (out_5, in_2, in_3);
  and and_1 (out_6, in_1, in_3);
endmodule
